// Logisim project problem4_ver.circ as structural Verilog
module main (
  input  in_1,
  input  in_2,
  input  in_3,
  output out_4,
  output out_5
);

  problem4 problem4_1 (.J(in_1), .K(in_2), .clk(in_3), .Q(out_4), .Q_bar(out_5));
endmodule

// VHDL entity problem4, as the project stores it:
library IEEE;
use IEEE.STD_LOGIC_1164.ALL;

entity problem4 is
    Port (
        J     : in  STD_LOGIC;
        K     : in  STD_LOGIC;
        clk   : in  STD_LOGIC;
        Q     : out STD_LOGIC;
        Q_bar : out STD_LOGIC
    );
end problem4;

architecture Behavioral of problem4 is
    signal q_reg : STD_LOGIC := '0';
begin

    process(clk)
    begin
        if rising_edge(clk) then
            if J = '0' and K = '0' then
                -- Hold
                null;

            elsif J = '0' and K = '1' then
                -- Reset
                q_reg <= '0';

            elsif J = '1' and K = '0' then
                -- Set
                q_reg <= '1';

            elsif J = '1' and K = '1' then
                -- Toggle
                q_reg <= not q_reg;
            end if;
        end if;
    end process;

    Q     <= q_reg;
    Q_bar <= not q_reg;

end Behavioral;
